# Fritzing sketch infra_matika (saved by Fritzing 0.9.2b)
breadboards: 1

parts:
  LCD1 = LCD screen
  Part1 = Arduino Uno (Rev3)
  R1 = Resistor [tolerance=±5% resistance=330 package="0402 [SMD]"]
  R2 = Rotary Potentiometer (Large) [maximum_resistance=10kΩ package=THT]
  LED1 = smd LED [color="Red (633nm)" package="1206 [SMD]"]
  LED2 = smd LED [color="Green (555nm)" package="1206 [SMD]"]
  R3 = Resistor [tolerance=±5% resistance=330 package="0805 [SMD]"]
  R4 = Resistor [tolerance=±5% resistance=330 package="0805 [SMD]"]
  IR1 = TSOP312.., 314.. [package=THT]

nets:
  VSS: LCD1.VSS, LCD1.R/W, LCD1.LED-, Part1.GND, R2.leg1, LED1.cathode, LED2.cathode, IR1.Vs
  VDD: LCD1.VDD, Part1.5V, R2.leg2, IR1.Data
  N1: LCD1.V0, R2.wiper
  N2: LCD1.RS, Part1.D12/MISO
  N3: LCD1.E, Part1.D11_PWM/MOSI
  N4: LCD1.DB4, Part1.D5_PWM
  N5: LCD1.DB5, Part1.D4
  N6: LCD1.DB6, Part1.D3_PWM
  N7: LCD1.DB7, Part1.D2
  N8: LCD1.LED+, R1.Pin_1
  N9: Part1.D9_PWM, R3.Pin_1
  N10: Part1.D10_PWM/SS, R4.Pin_1
  N11: Part1.D13/SCK, IR1.GND
  N12: LED1.anode, R3.Pin_0
  N13: LED2.anode, R4.Pin_0
