# Fritzing sketch joystick (saved by Fritzing 0.9.2b)
breadboards: 1

parts:
  Part1 = Arduino Uno (Rev3)
  OLED_I2C1 = OLED 128x64 I2C Monochrome Display
  Part2 = Thumb Joystick

nets:
  N1: Part1.A0, Part2.VERT
  N2: Part1.A1, Part2.HORZ
  N3: Part1.A4/SDA, OLED_I2C1.SDA
  N4: Part1.A5/SCL, OLED_I2C1.SCK
  N5: Part1.D7, Part2.SEL
  5V: Part1.5V, OLED_I2C1.VDD, Part2.VCC
  GND: Part1.GND, OLED_I2C1.GND, Part2.GND
