# Fritzing sketch robopixle_bt (saved by Fritzing 0.9.2b)

parts:
  VCC1 = Battery
  M1 = DC Motor
  M2 = DC Motor
  Part1 = Arduino Uno (Rev3)
  Part2 = Bluetooth HC-06
  U1 = SWITCH_SPDT [package=kps-1290]
  S1 = H-Bridge with L298N

nets:
  GND: VCC1.-, Part1.GND, Part2.GND, S1.GND
  N1: VCC1.+, U1.O
  N2: M1.pin_1, S1.M1-02
  N3: M1.pin_2, S1.M1-01
  N4: M2.pin_1, S1.M2-02
  N5: M2.pin_2, S1.M2-01
  N6: Part1.D8, S1.IN4
  N7: Part1.D9_PWM, S1.ENB
  N8: Part1.D2, Part2.TXD
  N9: Part1.D3_PWM, Part2.RXD
  N10: Part1.D4, S1.IN2
  N11: Part1.D5_PWM, S1.IN1
  N12: Part1.D6_PWM, S1.ENA
  N13: Part1.D7, S1.IN3
  5V: Part1.5V, Part2.VCC
  VIN: Part1.VIN, U1.P, U1.S, S1.12V

custom parts:
  Battery: Your standard 2x 18650 battery pack (7,4 Volts)
  H-Bridge with L298N: h-bridge
