# Fritzing sketch meric_stromku (saved by Fritzing 0.9.2b)
breadboards: 1

parts:
  PART1 = SparkFun Soil Moisture Sensor [part_number=SEN-13322]
  Part1 = Arduino Uno (Rev3)
  LED1 = smd LED [color="Green (555nm)" package="0603 [SMD]"]
  LED2 = smd LED [color="Green (555nm)" package="0603 [SMD]"]
  LED3 = smd LED [color="Green (555nm)" package="0603 [SMD]"]
  LED4 = smd LED [color="Green (555nm)" package="0603 [SMD]"]
  LED5 = smd LED [color="Red (633nm)" package="0603 [SMD]"]
  LED6 = smd LED [color="Red (633nm)" package="0603 [SMD]"]
  LED8 = smd LED [color="Red (633nm)" package="0603 [SMD]"]
  LED7 = smd LED [color="Red (633nm)" package="0603 [SMD]"]
  R1 = Resistor [tolerance=±5% resistance=220 package="1206 [SMD]"]
  R2 = Resistor [tolerance=±5% resistance=220 package="2010 [SMD]"]

nets:
  N1: PART1.VCC, Part1.D10_PWM/SS
  GND: PART1.GND, Part1.GND, LED1.cathode, LED2.cathode, LED3.cathode, LED4.cathode, LED5.cathode, LED6.cathode, LED8.cathode, LED7.cathode
  N2: PART1.SIG, Part1.A0
  N3: Part1.D8, R1.Pin_1
  N4: Part1.D9_PWM, R2.Pin_1
  N5: LED1.anode, LED2.anode, LED3.anode, LED4.anode, R1.Pin_0
  N6: LED5.anode, LED6.anode, LED8.anode, LED7.anode, R2.Pin_0

custom parts:
  SparkFun Soil Moisture Sensor: The SparkFun Soil Moisture Sensor is a simple breakout for measuring the moisture in soil and similar materials.
