# Fritzing sketch meric_vlhkosti_pudy (saved by Fritzing 0.9.2b)
breadboards: 1

parts:
  PART1 = SparkFun Soil Moisture Sensor [part_number=SEN-13322]
  OLED_I2C1 = OLED 128x64 I2C Monochrome Display
  Part1 = Arduino Uno (Rev3)

nets:
  VCC: PART1.VCC, OLED_I2C1.VDD, Part1.5V
  GND: PART1.GND, OLED_I2C1.GND
  N1: PART1.SIG, Part1.A0
  N2: OLED_I2C1.SDA, Part1.A5/SCL
  N3: OLED_I2C1.SCK, Part1.A4/SDA

custom parts:
  SparkFun Soil Moisture Sensor: The SparkFun Soil Moisture Sensor is a simple breakout for measuring the moisture in soil and similar materials.
