# Fritzing sketch meric_vzdalenosti (saved by Fritzing 0.9.2b)
breadboards: 1

parts:
  Part1 = Arduino Uno (Rev3)
  OLED_I2C1 = OLED 128x64 I2C Monochrome Display
  Part2 = SRF05 Ultrasonic Rangefinder

nets:
  N1: Part1.A4/SDA, OLED_I2C1.SDA
  N2: Part1.A5/SCL, OLED_I2C1.SCK
  N3: Part1.D12/MISO, Part2.Echo
  N4: Part1.D13/SCK, Part2.Trig
  5V: Part1.5V, OLED_I2C1.VDD, Part2.VCC
  GND: Part1.GND, OLED_I2C1.GND, Part2.GND
