# Fritzing sketch nepriblizuj_se (saved by Fritzing 0.9.2b)
breadboards: 1

parts:
  SP1 = SPEAKER [package=pcb_mount_speaker]
  Part1 = Arduino Uno (Rev3)
  DFPlayer_Mini1 = DFPlayer MINI [package="DIP (Dual Inline) [THT]"]
  R1 = Resistor [tolerance=±5% resistance=1k package=THT]  # not connected
  Part2 = SRF05 Ultrasonic Rangefinder

nets:
  N1: SP1.+, DFPlayer_Mini1.SPK2
  N2: SP1.-, DFPlayer_Mini1.SPK1
  N3: Part1.D10_PWM/SS, DFPlayer_Mini1.TX
  N4: Part1.D12/MISO, Part2.Trig
  N5: Part1.D13/SCK, Part2.Echo
  VCC: Part1.5V, DFPlayer_Mini1.VCC, Part2.VCC
  GND: Part1.GND, DFPlayer_Mini1.GND#6, Part2.GND

custom parts:
  DFPlayer MINI: MP3 module by DFRobot.com for playing Music from an SD-Card. Supports WAV and MP3 files.
