# Fritzing sketch rucni_blikac (saved by Fritzing 0.9.2b)
breadboards: 1

parts:
  S1 = Pushbutton [package="[SMD]"]
  LED1 = LED - 3mm [color="Red (633nm)" package="3 mm [THT]"]
  S2 = Pushbutton [package="[SMD]"]
  LED3 = LED - 3mm [color="Yellow (585nm)" package="3 mm [THT]"]
  Part1 = Arduino Uno (Rev3) - ICSP
  LED4 = LED - 3mm [color="White (6500K)" package="3 mm [THT]"]
  R2 = Resistor [tolerance=±5% resistance=220 package="0603 [SMD]"]
  R3 = Resistor [tolerance=±5% resistance=220 package="0603 [SMD]"]
  R4 = Resistor [tolerance=±5% resistance=220 package="0603 [SMD]"]
  LED5 = LED - 3mm [color="Red (633nm)" package="3 mm [THT]"]
  R5 = Resistor [tolerance=±5% resistance=220 package="1206 [SMD]"]

nets:
  N1: S1.Pin_1, S1.Pin_2, S1.Pin_3, S1.Pin_4, LED1.anode, R4.Pin_1
  N2: LED1.cathode, LED5.cathode
  N3: S2.Pin_1, S2.Pin_2, S2.Pin_3, S2.Pin_4, LED5.anode, R5.Pin_1
  N4: LED3.cathode, Part1.GND, LED4.cathode
  N5: LED3.anode, R3.Pin_1
  N6: Part1.5V, R2.Pin_0, R3.Pin_0
  N7: LED4.anode, R2.Pin_1
