# Fritzing sketch semafor (saved by Fritzing 0.9.2b)
breadboards: 1

parts:
  LED1 = LED - 5mm [color="Green (560nm)" package="5 mm [THT]"]
  LED2 = LED - 5mm [color="Yellow (595nm)" package="5 mm [THT]"]
  LED3 = LED - 5mm [color="Red (633nm)" package="5 mm [THT]"]
  Part1 = Arduino Uno (Rev3) - ICSP
  LED4 = LED - 5mm [color="Red (633nm)" package="5 mm [THT]"]
  LED5 = LED - 5mm [color="Green (560nm)" package="5 mm [THT]"]
  R1 = Resistor [tolerance=±5% resistance=330 package="2512 [SMD]"]
  R2 = Resistor [tolerance=±5% resistance=330 package="2512 [SMD]"]
  R3 = Resistor [tolerance=±5% resistance=330 package="2512 [SMD]"]
  R4 = Resistor [tolerance=±5% resistance=330 package="2512 [SMD]"]
  R5 = Resistor [tolerance=±5% resistance=330 package="2512 [SMD]"]

nets:
  N1: LED1.cathode, R1.Pin_0
  N2: LED1.anode, Part1.D8
  N3: LED2.cathode, R2.Pin_0
  N4: LED2.anode, Part1.D9_PWM
  N5: LED3.cathode, R3.Pin_0
  N6: LED3.anode, Part1.D10_PWM/SS
  N7: Part1.ICSP_MISO, Part1.D12/MISO, LED5.anode
  N8: Part1.ICSP_MOSI, Part1.D11_PWM/MOSI, LED4.anode
  N9: Part1.GND, R1.Pin_1, R2.Pin_1, R3.Pin_1, R4.Pin_0, R5.Pin_0
  N10: LED4.cathode, R4.Pin_1
  N11: LED5.cathode, R5.Pin_1
