# Fritzing sketch teplomer (saved by Fritzing 0.9.2b)
breadboards: 1

parts:
  Part1 = Arduino Uno (Rev3)
  U1 = 74HC595 [package="DIP16 [THT]"]
  T1 = LM35 Temperature Sensor [package="TO92 [THT]"]
  7_Segment1 = 7 Segment Display
  7_Segment2 = 7 Segment Display
  7_Segment3 = 7 Segment Display
  7_Segment4 = 7 Segment Display
  R1 = Resistor [tolerance=±5% resistance=220 package="1206 [SMD]"]
  R2 = Resistor [tolerance=±5% resistance=220 package="1206 [SMD]"]
  R3 = Resistor [tolerance=±5% resistance=220 package="1206 [SMD]"]
  R4 = Resistor [tolerance=±5% resistance=220 package="1206 [SMD]"]
  R5 = Resistor [tolerance=±5% resistance=220 package="1206 [SMD]"]
  R6 = Resistor [tolerance=±5% resistance=220 package="1206 [SMD]"]
  R7 = Resistor [tolerance=±5% resistance=220 package="1206 [SMD]"]
  R8 = Resistor [tolerance=±5% resistance=220 package="1206 [SMD]"]

nets:
  N1: Part1.A0, T1.Vout
  N2: Part1.D10_PWM/SS, U1.SH_CP
  N3: Part1.D11_PWM/MOSI, U1.ST_CP
  N4: Part1.D12/MISO, U1.Q0, R1.Pin_0
  N5: Part1.D6_PWM, 7_Segment3.Segment_G, 7_Segment3.Segment_F
  5V: Part1.5V, U1.MR, U1.VCC, T1.+Vs
  GND: Part1.GND, U1.GND, U1.OE, T1.GND
  N6: U1.Q1, R3.Pin_1
  N7: U1.Q2, 7_Segment3.Segment_DP, R7.Pin_1
  N8: U1.Q3, R5.Pin_0
  N9: U1.Q4, 7_Segment1.Segment_D, R4.Pin_0
  N10: U1.Q5, 7_Segment1.Segment_B, 7_Segment1.Segment_A, R2.Pin_0
  N11: U1.Q6, 7_Segment4.Segment_D, R8.Pin_1
  N12: U1.Q7, R6.Pin_0
  N13: 7_Segment1.Segment_G, 7_Segment1.Segment_F
  N14: 7_Segment2.Segment_G, 7_Segment2.Segment_F
  N15: 7_Segment2.Segment_D, R4.Pin_1
  N16: 7_Segment2.Segment_DP, R7.Pin_0
  N17: 7_Segment2.Segment_B, 7_Segment2.Segment_A, R2.Pin_1
  N18: 7_Segment3.Segment_D, R8.Pin_0
  N19: 7_Segment3.Segment_B, 7_Segment3.Segment_A
  N20: 7_Segment4.Segment_G, 7_Segment4.Segment_F
  N21: 7_Segment4.Segment_B, 7_Segment4.Segment_A

notes:
  330 ohm
  4 digit 7 segment 3461BS
