# Fritzing sketch touchduino (saved by Fritzing 0.9.2b)
breadboards: 1

parts:
  Part2 = Arduino Uno (Rev3)
  R1 = Resistor [tolerance=±5% resistance=2M package="0402 [SMD]"]
  R2 = Resistor [tolerance=±5% resistance=2M package="0402 [SMD]"]
  R3 = Resistor [tolerance=±5% resistance=2M package="0402 [SMD]"]
  R4 = Resistor [tolerance=±5% resistance=2M package="0402 [SMD]"]
  R5 = Resistor [tolerance=±5% resistance=2M package="0402 [SMD]"]
  R6 = Resistor [tolerance=±5% resistance=2M package="0402 [SMD]"]

nets:
  N1: Part2.A0, R1.Pin_1
  N2: Part2.A1, R2.Pin_1
  N3: Part2.A2, R3.Pin_1
  N4: Part2.A3, R4.Pin_1
  N5: Part2.A4/SDA, R5.Pin_1
  N6: Part2.A5/SCL, R6.Pin_1
  N7: Part2.ioref, R1.Pin_0, R2.Pin_0, R3.Pin_0, R4.Pin_0, R5.Pin_0, R6.Pin_0
